// Logisim project domaci_zadatak.circ as structural Verilog: 1 circuit, main circuit domaci_zadatak_2
module domaci_zadatak_2 (
  input  X1,
  input  X2,
  input  X3,
  input  X4,
  input  X5,
  output out_6
);

  wire nor_1_out, nor_2_out, nor_3_out, nor_4_out, nor_5_out, nor_6_out, nor_7_out;

  nor nor_1 (nor_1_out, X4, X5);
  nor nor_2 (nor_2_out, X1, X2);
  nor nor_3 (nor_3_out, nor_2_out, nor_2_out);
  nor nor_4 (nor_4_out, X3, X3);
  nor nor_5 (nor_5_out, nor_1_out, nor_1_out);
  nor nor_6 (nor_6_out, nor_3_out, nor_4_out);
  nor nor_7 (nor_7_out, nor_6_out, nor_6_out);
  nor nor_8 (out_6, nor_7_out, nor_5_out);

  // Notes on the sheet:
  //   00100
  //   Datum rodjenja 21.01
endmodule
